# Fritzing sketch Circuit (saved by Fritzing 0.9.5d)
breadboards: 1

parts:
  M1 = DOIT Esp32 DevKit v1 (30 pins long, 11 pins width) [part_number=ESP32S-PIN30]
  U1 = MPU 9250 Breakout [package="SIP (Single Inline) [THT]"]

nets:
  3V3: M1.3V3, U1.VCC
  GND: M1.GND, U1.GND
  N1: M1.D21, U1.SDA
  N2: M1.D22, U1.SCL

custom parts:
  DOIT Esp32 DevKit v1 (30 pins long, 11 pins width): The DOIT Esp32 DevKit v1 is one of the development board created by DOIT to evaluate the ESP-WROOM-32 module. It is based on the ESP32 microcontroller that boasts Wifi, Bluetooth, Ethernet and Low Power support all in a single chip. (vanepp) made breadboard work, adjusted pin numbering and labels and reduced size of schematic and cleaned up pcb. This chip is 30pins long (2 x15) and 11 pins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
  MPU 9250 Breakout: Generic MPU 9250 Breakout Board
